# Fritzing sketch CO2_Meter_V1 (saved by Fritzing 0.9.4)

parts:
  Display = AZ 1.3 inch OLED
  Sensor = SCD30
  Wago = 3x WAGO 221
  Wago_2 = 3x WAGO 221
  Wago_3 = 3x WAGO 221
  Ampel = LED Traffic Light
  U1 = NodeMCU V1.0

nets:
  N1: Display.SDA, Wago_2.T1
  N2: Display.SCK, Wago_3.T2
  GND: Display.GND, Sensor.GND, Ampel.GND, U1.GND
  N3: Display.VDD, Wago.T3
  N4: Sensor.VDD, Wago.T1
  N5: Sensor.TX/SCL, Wago_3.T1
  N6: Sensor.RX/SDA, Wago_2.T2
  N7: Wago.T2, U1.Vin
  N8: Wago_2.T3, U1.D2
  N9: Wago_3.T3, U1.D1
  N10: Ampel.G, U1.D8
  N11: Ampel.Y, U1.D7
  N12: Ampel.R, U1.D4

notes:
  red
  orange
  yellow
  green
  blue
  violet
  white
  black
  gray

custom parts:
  AZ 1.3 inch OLED: Monochrom OLED Display with a SSD1106 controller
  SCD30: CO2 , humidity, and temperature sensor * Current consumption: 19 mA @ 1 meas. per 2 s. * Digital interface UART or I2C * Company: Sensirion - The Sensor Company Electrical specifications * average current: 19 mA * max. current: 75 mA * DC supply: 3.3 V - 5.5 V Operation conditions * temperature: 0 – 50°C * humidity: 0 – 95 %RH * sensor lifetime: 15 years CO2-sensor: * NDIR CO 2 sensor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
  3x WAGO 221: WAGO 221 3x
  LED Traffic Light: RYG Traffic Light
  NodeMCU V1.0: ESP8266 based NodeMCU
