# Fritzing sketch CO2_Meter_V1_w_RTC (saved by Fritzing 0.9.4)

parts:
  Ampel = LED Traffic Light
  Display = AZ 1.3 inch OLED
  ZS-042_RTC1 = ZS-042 RTC Module
  T1 = 5x WAGO 221
  T2 = 5x WAGO 221
  U1 = NodeMCU V1.0
  Sensor = SCD30
  o1 = Module display OLED I2C 128x64 SSD1306 [package=THT]
  T4 = 3x WAGO 221

nets:
  N1: Ampel.G, U1.D8
  N2: Ampel.Y, U1.D7
  N3: Ampel.R, U1.D4
  GND: Ampel.GND, Display.GND, ZS-042_RTC1.GND, U1.GND, Sensor.GND, o1.GND
  N4: Display.SDA, T2.T4, o1.SDA
  N5: Display.SCK, T1.T4, o1.SCL
  VDD: Display.VDD, o1.VCC, T4.T3
  VCC: ZS-042_RTC1.VCC, U1.3V3
  N6: ZS-042_RTC1.SDA, T2.T3
  N7: ZS-042_RTC1.SCL, T1.T3
  N8: T1.T2, Sensor.TX/SCL
  N9: T1.T5, U1.D1
  N10: T2.T2, Sensor.RX/SDA
  N11: T2.T5, U1.D2
  N12: U1.Vin, T4.T2
  N13: Sensor.VDD, T4.T1

notes:
  SCL/SCK:
  - red
  - orange
  - brown
  - yellow
  VCC / VIN:
  - green
  - blue
  - d.c.
  - violet
  SDA:
  - white
  - gray
  - d.c.
  - black
  (1)
  (2)
  (3)
  (6)
  (7)
  (9)
  (4)
  (5)
  (8)
  (10)
  (d.c.) = Farbe egal
  1.3" Display
  (alternativ)
  0.96" Display
  Dieses Teil entfernen!!
  Remove this part!!

custom parts:
  LED Traffic Light: RYG Traffic Light
  AZ 1.3 inch OLED: Monochrom OLED Display with a SSD1106 controller
  5x WAGO 221: WAGO 221 5x
  NodeMCU V1.0: ESP8266 based NodeMCU
  SCD30: CO2 , humidity, and temperature sensor * Current consumption: 19 mA @ 1 meas. per 2 s. * Digital interface UART or I2C * Company: Sensirion - The Sensor Company Electrical specifications * average current: 19 mA * max. current: 75 mA * DC supply: 3.3 V - 5.5 V Operation conditions * temperature: 0 – 50°C * humidity: 0 – 95 %RH * sensor lifetime: 15 years CO2-sensor: * NDIR CO 2 sensor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
  Module display OLED I2C 128x64 SSD1306: Ecran OLED I2C SSD163 de 128x64 avec connexion I2C
  3x WAGO 221: WAGO 221 3x
