# Fritzing sketch CO2_Meter_V3 (saved by Fritzing 0.9.4)

parts:
  Prozessor = ESP8266 NodeMCU LoLin module
  Ampel = LED Traffic Light
  Display = AZ 1.3 inch OLED
  Sensor = SCD30
  Wago = 3x WAGO 221
  Wago_2 = 3x WAGO 221
  Wago_3 = 3x WAGO 221

nets:
  N1: Prozessor.D1, Wago_3.T3
  N2: Prozessor.D2, Wago_2.T3
  N3: Prozessor.D4, Ampel.R
  GND: Prozessor.GND, Ampel.GND, Display.GND, Sensor.GND
  N4: Prozessor.D7, Ampel.Y
  N5: Prozessor.D8, Ampel.G
  N6: Prozessor.VU, Wago.T2
  N7: Display.SDA, Wago_2.T1
  N8: Display.SCK, Wago_3.T2
  N9: Display.VDD, Wago.T3
  N10: Sensor.VDD, Wago.T1
  N11: Sensor.TX/SCL, Wago_3.T1
  N12: Sensor.RX/SDA, Wago_2.T2

notes:
  red
  orange
  yellow
  green
  blue
  violet
  white
  black
  gray

custom parts:
  ESP8266 NodeMCU LoLin module: ESP8266 based NodeMCU
  LED Traffic Light: RYG Traffic Light
  AZ 1.3 inch OLED: Monochrom OLED Display with a SSD1106 controller
  SCD30: CO2 , humidity, and temperature sensor * Current consumption: 19 mA @ 1 meas. per 2 s. * Digital interface UART or I2C * Company: Sensirion - The Sensor Company Electrical specifications * average current: 19 mA * max. current: 75 mA * DC supply: 3.3 V - 5.5 V Operation conditions * temperature: 0 – 50°C * humidity: 0 – 95 %RH * sensor lifetime: 15 years CO2-sensor: * NDIR CO 2 sensor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
  3x WAGO 221: WAGO 221 3x
