# Fritzing sketch CO2_Meter_V3_w_RTC (saved by Fritzing 0.9.4)

parts:
  Prozessor = ESP8266 NodeMCU LoLin module
  Ampel = LED Traffic Light
  Display = AZ 1.3 inch OLED
  Sensor = SCD30
  ZS-042_RTC1 = ZS-042 RTC Module
  T1 = 5x WAGO 221
  T2 = 5x WAGO 221
  o1 = Module display OLED I2C 128x64 SSD1306 [package=THT]
  T5 = 3x WAGO 221

nets:
  N1: Prozessor.D1, T1.T5
  N2: Prozessor.D2, T2.T5
  N3: Prozessor.D4, Ampel.R
  3V3: Prozessor.3V3, ZS-042_RTC1.VCC
  GND: Prozessor.GND, Ampel.GND, Display.GND, Sensor.GND, ZS-042_RTC1.GND, o1.GND
  N4: Prozessor.D7, Ampel.Y
  N5: Prozessor.D8, Ampel.G
  N6: Prozessor.VU, T5.T2
  N7: Display.SDA, T2.T4, o1.SDA
  N8: Display.SCK, T1.T4, o1.SCL
  VDD: Display.VDD, o1.VCC, T5.T3
  N9: Sensor.VDD, T5.T1
  N10: Sensor.TX/SCL, T1.T2
  N11: Sensor.RX/SDA, T2.T2
  N12: ZS-042_RTC1.SDA, T2.T3
  N13: ZS-042_RTC1.SCL, T1.T3

notes:
  (1)
  (7)
  (10)
  (9)
  (6)
  (2)
  (8)
  (3)
  (d.c.) = Farbe egal
  (4)
  (5)
  SDA:
  - white
  - gray
  - d.c.
  - black
  SCL/SCK:
  - red
  - orange
  - brown
  - yellow
  VCC / VU:
  - green
  - blue
  - d.c.
  - violet
  1.3" Display
  (alternativ)
  0.96" Display
  Dieses Teil entfernen!!
  Remove this part!!

custom parts:
  ESP8266 NodeMCU LoLin module: ESP8266 based NodeMCU
  LED Traffic Light: RYG Traffic Light
  AZ 1.3 inch OLED: Monochrom OLED Display with a SSD1106 controller
  SCD30: CO2 , humidity, and temperature sensor * Current consumption: 19 mA @ 1 meas. per 2 s. * Digital interface UART or I2C * Company: Sensirion - The Sensor Company Electrical specifications * average current: 19 mA * max. current: 75 mA * DC supply: 3.3 V - 5.5 V Operation conditions * temperature: 0 – 50°C * humidity: 0 – 95 %RH * sensor lifetime: 15 years CO2-sensor: * NDIR CO 2 sensor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
  5x WAGO 221: WAGO 221 5x
  Module display OLED I2C 128x64 SSD1306: Ecran OLED I2C SSD163 de 128x64 avec connexion I2C
  3x WAGO 221: WAGO 221 3x
